# Fritzing sketch PoissonAby (saved by Fritzing 0.9.3b)
breadboards: 1

parts:
  Composant1 = Arduino Uno (Rev3)
  R1 = Photocell (LDR) [package=THT]
  R2 = Resistor [tolerance=±5% resistance=10k package=THT]
  LED1 = LED - 5mm [color="Red (633nm)" package="5 mm [THT]"]

nets:
  N1: Composant1.A0, R1.pin_0, R2.Pin_1
  N2: Composant1.GND, R2.Pin_0, LED1.cathode
  N3: Composant1.D2, LED1.anode
  N4: Composant1.5V, R1.pin_1
